# Fritzing sketch Controller (saved by Fritzing 0.9.2b)
circuit board: 8.46667cm x 5.64444cm
breadboards: 1

parts:
  Arduino_Uno = Arduino Uno (Rev3)
  Main_Drive_Motors = DC Motor
  U6 = RELAY [package=relay-g5q]
  U7 = RELAY [package=relay-g5q]
  U8 = RELAY [package=relay-g5q]
  U9 = RELAY [package=relay-g5q]
  Steering_Motor = DC Motor
  RS232_to_TTL = RS232 Transceiver [package=so016]
  DB9 = DB9 Connector [package=db9]
  C1 = Ceramic Capacitor [capacitance=0.1µF package="1206 [SMD, multilayer]"]
  C2 = Ceramic Capacitor [capacitance=0.1µF package="1206 [SMD, multilayer]"]
  C3 = Ceramic Capacitor [capacitance=0.1µF package="1206 [SMD, multilayer]"]

nets:
  GND: Arduino_Uno.GND, U6.NC, U6.COIL1, U7.NC, U7.COIL1, U8.NC, U8.COIL1, U9.NC, U9.COIL1, RS232_to_TTL.GND, DB9.5
  N1: Arduino_Uno.D0/RX, RS232_to_TTL.R1OUT
  N2: Arduino_Uno.D1/TX, RS232_to_TTL.T1IN
  N3: Arduino_Uno.D2, U6.COIL2
  N4: Arduino_Uno.D3_PWM, U7.COIL2
  N5: Arduino_Uno.D4, U8.COIL2
  N6: Arduino_Uno.D5_PWM, U9.COIL2
  5V: Arduino_Uno.VIN, RS232_to_TTL.VCC
  N7: Main_Drive_Motors.pin_1, U7.MAIN
  N8: Main_Drive_Motors.pin_2, U6.MAIN
  12V: U6.NO, U7.NO, U8.NO, U9.NO
  N9: U8.MAIN, Steering_Motor.pin_2
  N10: U9.MAIN, Steering_Motor.pin_1
  N11: RS232_to_TTL.C1+, C1.1
  N12: RS232_to_TTL.V+, C3.1
  N13: RS232_to_TTL.C1-, C1.0
  N14: RS232_to_TTL.C2+, C2.1
  N15: RS232_to_TTL.C2-, C2.0
  N16: RS232_to_TTL.V-, C3.0
  N17: RS232_to_TTL.R1IN, DB9.3
  N18: RS232_to_TTL.T1OUT, DB9.2
